# Fritzing sketch Minecraft - Find a Block (saved by Fritzing 0.9.3b)
breadboards: 1

parts:
  Raspberry_Pi_1 = Raspberry Pi 3 [part_number=RPI-3-V1.2]
  LED1 = LED - 5mm [color="Red (633nm)" package="5 mm [THT]"]
  J1 = Piezo Speaker
  R1 = Resistor [tolerance=±5% resistance=220 package=THT]

nets:
  N1: Raspberry_Pi_1.GPIO17, J1.pin2
  N2: Raspberry_Pi_1.GPIO24, LED1.anode
  N3: Raspberry_Pi_1.GND, J1.pin1, R1.Pin_1
  N4: LED1.cathode, R1.Pin_0
