# Fritzing sketch Python Sorting Hat Wiring (saved by Fritzing 0.9.3b)
breadboards: 1

parts:
  Raspberry_Pi_1 = Raspberry Pi 3 [part_number=RPI-3-V1.2]
  S1 = Pushbutton [package="[THT]"]

nets:
  N1: Raspberry_Pi_1.GND, S1.Pin_4
  N2: Raspberry_Pi_1.GPIO17, S1.Pin_2
