# Fritzing sketch temp sensor (saved by Fritzing 0.9.3b)
breadboards: 1

parts:
  Raspberry_Pi_1 = Raspberry Pi 3 [part_number=RPI-3-V1.2]
  R1 = Resistor [tolerance=±5% resistance=4.7k package=THT]
  J1 = screw terminal, 3 pins
  DS1 = DS18B20 1-Wire Temperature Sensor [part_number=DS18B20]  # not connected

nets:
  N1: Raspberry_Pi_1.3v3, R1.Pin_0, J1.pin1
  N2: Raspberry_Pi_1.GPIO4, R1.Pin_1, J1.pin2
  N3: Raspberry_Pi_1.GND, J1.pin3
