# Fritzing sketch lisiparoi 1 (saved by Fritzing 0.9.3b)
breadboards: 1

parts:
  Raspberry_Pi_1 = Raspberry Pi 3 [part_number=RPI-3-V1.2]
  Lisiparoi1 = Lisiparoi v1.0 Infra Red

nets:
  N1: Raspberry_Pi_1.GPIO2, Lisiparoi1.GPIO
  GND: Raspberry_Pi_1.GND, Lisiparoi1.GND1
  5V: Raspberry_Pi_1.5V, Lisiparoi1.5V

custom parts:
  Lisiparoi v1.0 Infra Red: Infra Red LED halo for Raspberry Pi Camera
